# Fritzing sketch TT Robot (saved by Fritzing 0.9.1b)
breadboards: 1

parts:
  J1 = Basic Servo
  J2 = Basic Servo
  J3 = Basic Servo
  Part1 = Arduino Uno (Rev3)
  C1 = Tantalum Capacitor [capacitance=1μF package="100 mil [THT, tantalum]"]
  C2 = Tantalum Capacitor [capacitance=1μF package="100 mil [THT, tantalum]"]
  C3 = Tantalum Capacitor [capacitance=1μF package="100 mil [THT, tantalum]"]
  VCC1 = Battery block 9V  # not connected

nets:
  GND: J1.gnd, J2.gnd, J3.gnd, Part1.GND, C1.-, C2.-, C3.-
  VCC: J1.vcc, J2.vcc, J3.vcc, Part1.5V, C1.+, C2.+, C3.+
  N1: J1.pulse, Part1.D6_PWM
  N2: J2.pulse, Part1.D5_PWM
  N3: J3.pulse, Part1.D10_PWM/SS

notes:
  9V Battery to power the Arduino Uno (Voltage regulator integrated in the Arduino to convert 9V into the needed 5V for the motors to function)
  Added capacitors to prevent any delays or noises
  The address spaces used are 10 (pen servo motor), 5 (right servo motor), 6 (left servo motor)
  Red wire = 5V (used to power servo motors)
  Black wire = ground
  Right Wheel
  Left wheel
  Pen Mount
